# Fritzing sketch ga-lamp (saved by Fritzing 0.7.9b)
breadboards: 1

parts:
  Arduino1 = Arduino
  LED1 = RGB LED (com. anode, rbg) [package="5 mm [THT]"]
  part = Resistor [tolerance=±5% resistance=220 package=THT]  # not connected
  R1 = Resistor [tolerance=±5% resistance=220 package=THT]
  R2 = Resistor [tolerance=±5% resistance=220 package=THT]
  R3 = Resistor [tolerance=±5% resistance=220 package=THT]

nets:
  N1: Arduino1.D12, R3.Pin_1
  N2: Arduino1.D9, R1.Pin_1
  N3: LED1.red_cathode, R1.Pin_0
  N4: LED1.blue_cathode, R2.Pin_0
  N5: LED1.green_cathode, R3.Pin_0
